// Digital circuit CORE.dig as structural Verilog
module CORE (
  input  clk,
  input  RST,
  input  CLR,
  input  in_4,
  input  [11:0] MIPCBI,
  input  [15:0] PCBI,
  input  MIPCBE,
  input  PCBE
);

  wire ALUD_CO, and_2_out, and_3_out, ASSERT_p5, BR_CPLQ, BR_Q, button_1_out, CLK_t, CLKR, comparator_1_eq,
       comparator_1_gt, comparator_1_lt, comparator_2_eq, comparator_3_eq, decoder_1_out_0, decoder_1_out_1,
       decoder_1_out_2, decoder_1_out_3, decoder_1_out_4, decoder_1_out_5, decoder_1_out_6, decoder_1_out_7,
       DIRECT_OE, DIRECT_WE, DPC_JUMP, DUMP_p5, EXT_p5, IRQ_CLR, IRQ_OE, nALUDH_OE, nALUDL_OE, nALUS_OE,
       nCLR, nDPC_JUMP, nIMMED_OE, not_8_out, not_13_out, nRAM_OE, nROM_OE, nSFR_OE, nXRAM_OE, or_1_out,
       RAM_OE, RAM_WE, RF_SFR, RF_WE, RFSRCR_WE, SR_WE, WR_WE, XRAM_WE;
  wire [2:0] BR_SRC, BUS_SRC, JUMP_TYPE;
  wire [3:0] ALUSD_FUNC, multiplexer_2_out, RF_SRC;
  wire [4:4] multiplexer_2_out_2;
  wire [5:0] nand_1_out;
  wire [7:0] BUS_D, IMMED, RF_Q;
  wire [7:4] RFSRCR_q;
  wire [11:0] ADDRESS, MIPC;
  wire [15:0] ADDR_16, PCER_q;
  wire [47:46] DECODER_2_d;

  Comparator #(.Bits(8)) comparator_1 (
    .a(RF_Q), .b(IMMED), .gt(comparator_1_gt), .eq(comparator_1_eq), .lt(comparator_1_lt));
  Decoder #(.Selector_Bits(3)) decoder_1 (
    .sel(BUS_SRC), .out_0(decoder_1_out_0), .out_1(decoder_1_out_1), .out_2(decoder_1_out_2),
    .out_3(decoder_1_out_3), .out_4(decoder_1_out_4), .out_5(decoder_1_out_5), .out_6(decoder_1_out_6),
    .out_7(decoder_1_out_7));
  not not_1 (nALUS_OE, decoder_1_out_0);
  not not_2 (nALUDL_OE, decoder_1_out_1);
  not not_3 (nALUDH_OE, decoder_1_out_2);
  not not_4 (nIMMED_OE, decoder_1_out_3);
  not not_5 (nRAM_OE, decoder_1_out_4);
  not not_6 (nXRAM_OE, decoder_1_out_5);
  not not_7 (nROM_OE, decoder_1_out_6);
  not not_8 (not_8_out, decoder_1_out_7);
  DCOUTER #(.generic("Bits := 12;")) dcouter_1 (
    .CLK(CLK_t), .nCLR(nCLR), .CNT(1'b1), .nLE(nDPC_JUMP), .D(ADDRESS), .Q(MIPC));
  Multiplexer #(.Selector_Bits(3)) multiplexer_1 (
    .sel(JUMP_TYPE), .in_0(1'b0), .in_1(1'b1), .in_2(comparator_1_gt), .in_3(comparator_1_eq),
    .in_4(comparator_1_lt), .in_5(BR_Q), .in_6(RST), .in_7(1'b0), .out(DPC_JUMP));
  not not_9 (IRQ_OE, not_8_out);
  assign BUS_D = ~nIMMED_OE ? IMMED : 8'bz;  // DriverInvSel driverinvsel_1
  PullDown #(.Bits(8)) pulldown_1 (.out(BUS_D));
  assign BUS_D = ~nSFR_OE ? RF_Q : 8'bz;  // DriverInvSel driverinvsel_2
  PCE PCER (.CLK(CLK_t), .D(BUS_D), .RS(RF_SRC), .WE(RF_WE), .Q(PCER_q));
  not not_10 (nDPC_JUMP, DPC_JUMP);
  not not_11 (RAM_OE, nRAM_OE);
  // Probe on BUS_D
  ROM #(.AddrBits(12), .Bits(48)) DECODER_2 (
    .A(MIPC), .sel(1'b1),
    .D({DECODER_2_d, IMMED, ADDRESS, JUMP_TYPE, IRQ_CLR, ALUSD_FUNC, XRAM_WE, RAM_WE, RFSRCR_WE, BR_CPLQ, BR_SRC, SR_WE, WR_WE, BUS_SRC, RF_SFR, RF_WE, RF_SRC}));
  Register #(.Bits(8)) RFSRCR (.D(BUS_D), .C(CLK_t), .en(RFSRCR_WE), .Q({RFSRCR_q, nand_1_out[3:0]}));
  and and_1 (nand_1_out[4], RFSRCR_q[4], RAM_WE);
  nand nand_1 (nand_1_out[5], RFSRCR_q[4], RAM_OE);
  Comparator #(.Bits(12)) comparator_2 (.a(MIPCBI), .b(MIPC), .eq(comparator_2_eq));  // open: gt, lt
  Comparator #(.Bits(16)) comparator_3 (.a(PCBI), .b(PCER_q), .eq(comparator_3_eq));  // open: gt, lt
  and and_2 (and_2_out, comparator_2_eq, MIPCBE);
  and and_3 (and_3_out, comparator_3_eq, PCBE);
  Multiplexer #(.Bits(6)) multiplexer_2 (
    .sel(RF_SFR), .in_0({1'b1, RF_WE, RF_SRC}), .in_1(nand_1_out),
    .out({nSFR_OE, multiplexer_2_out_2[4], multiplexer_2_out}));
  // Probe on MIPC
  // Probe on RF_SRC
  // Probe on RF_WE
  // Probe on RF_SFR
  // Probe on BUS_SRC
  // Probe on WR_WE
  // Probe on SR_WE
  // Probe on BR_SRC
  // Probe on BR_CPLQ
  // Probe on RFSRCR_WE
  // Probe on RAM_WE
  // Probe on XRAM_WE
  // Probe on ALUSD_FUNC
  // Probe on IRQ_CLR
  // Probe on JUMP_TYPE
  // Probe on ADDRESS
  // Probe on IMMED
  // EXTCTL EXT: pin names not known; wires that end beside it: DIRECT_WE, ADDR_16[15:8], BUS_D, CLK_t, EXT_p5
  // ASSERT ASSERT: pin names not known; wires that end beside it: CLK_t, BUS_D, ADDR_16[15:8], DIRECT_WE, ASSERT_p5, CLK_t
  not not_12 (nCLR, CLR);
  Button button_1 (.out(button_1_out));
  reg_file RF (
    .CLK(CLK_t), .RS(multiplexer_2_out), .D(BUS_D), .LLE(multiplexer_2_out_2[4]),
    .HLE(multiplexer_2_out_2[4]), .Q(RF_Q));
  // Probe on EXT_p5
  // SwitchDT switchdt_1: pin names not known; wires that end beside it: clk, button_1_out, CLKR
  // Probe on RF_Q
  // DUMP DUMP: pin names not known; wires that end beside it: DIRECT_WE, ADDR_16[15:8], BUS_D, CLK_t, DUMP_p5
  or or_1 (or_1_out, ASSERT_p5, and_2_out, and_3_out);
  // Probe on DUMP_p5
  reg__sync_clear #(.generic("Bits := 8;")) WR (.D(BUS_D), .CLK(CLK_t), .CLR(CLR), .LE(WR_WE), .Q(ADDR_16[7:0]));
  reg__sync_clear #(.generic("Bits := 8;")) SR (.D(BUS_D), .CLK(CLK_t), .CLR(CLR), .LE(SR_WE), .Q(ADDR_16[15:8]));
  and and_4 (DIRECT_WE, RF_SFR, RAM_WE);
  and and_5 (DIRECT_OE, RF_SFR, RAM_OE);
  STALL STALL (.C(CLKR), .AC(or_1_out), .S(in_4), .OAC(CLK_t));  // open: G, nCLR, O
  INT INT (
    .CLK(CLK_t), .CLR(CLR), .A(ADDR_16[15:8]), .D(BUS_D), .WE(DIRECT_WE), .OE(DIRECT_OE), .IRQOE(IRQ_OE),
    .CII(IRQ_CLR));
  // Probe on ADDR_16[7:0]
  // Probe on ADDR_16[15:8]
  not not_13 (not_13_out, nROM_OE);
  ALU ALU (
    .A(RF_Q), .B(ADDR_16[7:0]), .S(ALUSD_FUNC), .CI(BR_Q), .nSOE(nALUS_OE), .nDLOE(nALUDL_OE),
    .nDHOE(nALUDH_OE), .O(BUS_D), .CO(ALUD_CO));
  ROM #(.AddrBits(16), .Bits(8)) ROM (.A(ADDR_16), .sel(not_13_out), .D(BUS_D));
  RAM RAM (.AC(CLK_t), .A(ADDR_16[15:8]), .WE(RAM_WE), .nOE(nRAM_OE), .Dt(RF_SFR), .O(BUS_D));
  XRAM XRAM (.CLK(CLK_t), .A(ADDR_16), .WE(XRAM_WE), .nOE(nXRAM_OE), .O(BUS_D));
  BR BR (
    .CLK(CLK_t), .nCLR(nCLR), .S(BR_SRC), .I4(ALUD_CO), .I5(ALUD_CO), .I7(RF_Q[0]), .I6(RF_Q[7]),
    .CPQ(BR_CPLQ), .Q(BR_Q));

  // Other names for the same wires on the sheet: ADDR_RAM[7:0] = ADDR_16[15:8]; GO = in_4

  // Notes on the sheet:
  //   clk: Hz: 2147483647
  //   LS137/LS138
  //   LS161
  //   LS151/LS251
  //   contents of DECODER_2 (hex, n*v repeats v):
  //   eef100248,100449,19a,102886,381855,3c2a58,3c0459,20086e00000a,3002c600000a,38010e00000a,
  //   3c009e00000a,3e003e00000a,100245,34044a,eb0910046,3d007600000a,3d805600000a,100245,
  //   30044a,500,eb0910046,3d407200000a,59c,c800c,100246,151860,3c2858,eb0bc0059,eb0b80096,
  //   3c808e00000a,100245,30044a,300,4c0,eb0920046,3c0e8100000a,100241,100442,eb0920046,
  //   3a00ae00000a,100245,34044a,eb0800116,3900e600000a,3980c600000a,100245,30044a,500,
  //   eb0800116,3940e200000a,59c,c800c,320,141856,3c2858,eb0bc0059,eb08000d6,3880fe00000a,
  //   100245,30044a,300,4c0,eb0800156,380e6900000a,100241,100442,eb0800156,34020600000a,
  //   36014200000a,19c,100245,34044a,11d,25001d,4eaa00180d,101a4c,82858,3c1059,32cc,eb08c0059,
  //   3501a600000a,35816a00000a,100245,30044a,500,11c,100246,1d004c,10024c,eb09c0056,35419200000a,
  //   59c,c800c,320,14005d,24021d,150060,4ea2001acd,3c2a58,858bc0459,205,42856,1a2801800,
  //   eb0800000,eb0b00015,3481de00000a,34c1b600000a,1800,eb0b00015,39c,14005d,2c001d,28041c,
  //   c800c,1b20,18024d,151860,3c2858,eb0bc0059,340e8100000a,19c,100440,300,10044c,c800c,
  //   150060,241810,3c2858,eb0bc0059,32021e00000a,100245,34044a,300,110046,eb0940056,31026e00000a,
  //   31823e00000a,100245,30044a,500,100246,116,eb0950040,31426a00000a,59c,c800c,320,14005c,
  //   100246,150060,10024c,141856,3c2858,eb0bc0059,eb0bc0016,3082a600000a,30c27e00000a,
  //   1000,eb0b00015,39c,14005d,2c001d,28041c,c800c,1320,18024d,151860,3c2858,eb0bc0059,
  //   300e6900000a,59c,c800c,320,200410,151840,3c2858,eb0bc0059,2805be00000a,2c03f600000a,
  //   2e02fe00000a,19d,100245,34044a,11c,10124d,c2a5c,300015,14288c,4ea2801ac0,3c2a58,858bc0459,
  //   2d038200000a,2d833600000a,19d,100245,30044a,500,11c,10124d,c2a5c,300015,14288c,4ea2801ac0,
  //   3c2a58,858bc0459,2d436200000a,59c,c800c,1320,c2a46,300015,14005c,14288c,4ea2801ac0,
  //   3c2a58,858bc0459,1380,c2a46,300015,14005c,14288c,4ea2801ac0,3c2a58,858bc0459,2c83c200000a,
  //   2cc39200000a,382885,eb0b00015,39c,14005d,2c001d,28041c,c800c,320,1c288d,800,18024d,
  //   151860,3c2858,eb0bc0059,2c0e8100000a,39c,14005d,2c001d,28041c,c800c,320,1c009d,38028d,
  //   342885,301815,3c2858,eb0bc0059,2a041e00000a,59c,c800c,320,14005c,100245,34044a,11184c,
  //   3c2858,eb0bc0059,29054e00000a,29844e00000a,59c,c800c,320,14005c,100245,30044a,500,
  //   11184c,3c2858,eb0bc0059,29445200000a,10dc,44f6183816,81207,8285c,18381c,18101d,4502183816,
  //   81207,8285c,18381c,18101d,450a183816,81207,8285c,18381c,18101d,4512183816,81207,8285c,
  //   18381c,18101d,451a183816,81207,8285c,18381c,18101d,4522183816,81207,8285c,18381c,
  //   18101d,452a183816,81207,8285c,18381c,18101d,4532183816,81207,8285c,183a1c,53898101d,
  //   d6,10d7,eb0ac0055,18381c,18101d,18381c,18101d,18381c,18101d,18381c,18101d,18381c,
  //   18101d,18381c,18101d,183a1c,18101d,140057,142887,100a4d,140056,eb0ac0055,28858a00000a,
  //   28c56200000a,1800,3c2851,eb0bc0052,39c,14005d,2c001d,28041c,c800c,320,1c288d,301815,
  //   3c2858,eb0bc0059,280e6900000a,39c,14005d,2c001d,28041c,c800c,320,1c009d,38028d,302885,
  //   301815,3c2858,eb0bc0059,2406c200000a,2605ea00000a,103245,34044a,31d,c0286,14005c,
  //   20c,240055,10024d,eb08c0056,25066a00000a,25861a00000a,103245,30044a,500,31d,c0286,
  //   14005c,20c,240055,10024d,eb08c0056,25464a00000a,3005,59c,c800c,320,14005d,c0286,14005c,
  //   20c,240055,10024d,ea88c1856,3005,39d,c0286,14005c,20c,240055,10024d,ea88c1856,2486ae00000a,
  //   24c68200000a,101246,82a41,3c0442,eb0800196,3005,39c,14005d,2c001d,28041c,c800c,320,
  //   18024d,151860,3c2858,eb0bc0059,240e8100000a,1992,3c2a58,3c0459,ea8801991,2206e200000a,
  //   19c,100245,34044a,300,c800c,10044c,ea8951860,21081200000a,21871200000a,19c,100245,
  //   30044a,500,300,c800c,10044c,151860,3c2858,eb0bc0059,21473e00000a,59c,c800c,320,14185d,
  //   3c2a58,3c0459,59c,10024d,c800c,ea8951860,dc,480a101247,48021c3016,1c101c,c284c,75a801000,
  //   c185c,1c3016,1c101c,c284c,76e801000,c185c,1c3016,1c101c,c284c,782801000,c185c,1c3016,
  //   1c101c,c284c,796801000,c185c,1c3016,1c101c,c284c,7aa801000,c185c,1c3016,1c101c,c284c,
  //   7be801000,c185c,1c3016,1c101c,c284c,7d2801000,c185c,1c3016,1c101c,c284c,7f2801000,
  //   c1a5c,140057,1c1016,eb0ac0055,10024c,140057,1c1016,eb0ac0055,10d7,eb0ac0055,1800,
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  //   at28c64
  //   core is at28c64
  //   contents of ROM (hex, n*v repeats v):
  //   75,d0,0,75,0,ff,76,0,75,0,fe,76,0,75,0,fd,76,0,75,0,fc,76,0,75,0,fb,76,0,75,0,fa,
  //   76,0,75,0,f9,76,0,75,0,f8,76,0,75,0,f7,76,0,75,0,f6,76,0,75,0,f5,76,0,75,0,f4,76,
  //   0,75,0,f3,76,0,75,0,f2,76,0,75,0,f1,76,0,75,0,f0,76,0,75,0,ef,76,0,75,0,ee,76,0,75,
  //   0,ed,76,0,75,0,ec,76,0,75,0,eb,76,0,75,0,ea,76,0,75,0,e9,76,0,75,0,e8,76,0,75,0,e7,
  //   76,0,75,0,e6,76,0,75,0,e5,76,0,75,0,e4,76,0,75,0,e3,76,0,75,0,e2,76,0,75,0,e1,76,
  //   0,75,0,e0,76,0,75,0,df,76,0,75,0,de,76,0,75,0,dd,76,0,75,0,dc,76,0,75,0,db,76,0,75,
  //   0,da,76,0,75,0,d9,76,0,75,0,d8,76,0,75,0,d7,76,0,75,0,d6,76,0,75,0,d5,76,0,75,0,d4,
  //   76,0,75,0,d3,76,0,75,0,d2,76,0,75,0,d1,76,0,75,0,d0,76,0,75,0,cf,76,0,75,0,ce,76,
  //   0,75,0,cd,76,0,75,0,cc,76,0,75,0,cb,76,0,75,0,ca,76,0,75,0,c9,76,0,75,0,c8,76,0,75,
  //   0,c7,76,0,75,0,c6,76,0,75,0,c5,76,0,75,0,c4,76,0,75,0,c3,76,0,75,0,c2,76,0,75,0,c1,
  //   76,0,75,0,c0,76,0,75,0,bf,76,0,75,0,be,76,0,75,0,bd,76,0,75,0,bc,76,0,75,0,bb,76,
  //   0,75,0,ba,76,0,75,0,b9,76,0,75,0,b8,76,0,75,0,b7,76,0,75,0,b6,76,0,75,0,b5,76,0,75,
  //   0,b4,76,0,75,0,b3,76,0,75,0,b2,76,0,75,0,b1,76,0,75,0,b0,76,0,75,0,af,76,0,75,0,ae,
  //   76,0,75,0,ad,76,0,75,0,ac,76,0,75,0,ab,76,0,75,0,aa,76,0,75,0,a9,76,0,75,0,a8,76,
  //   0,75,0,a7,76,0,75,0,a6,76,0,75,0,a5,76,0,75,0,a4,76,0,75,0,a3,76,0,75,0,a2,76,0,75,
  //   0,a1,76,0,75,0,a0,76,0,75,0,9f,76,0,75,0,9e,76,0,75,0,9d,76,0,75,0,9c,76,0,75,0,9b,
  //   76,0,75,0,9a,76,0,75,0,99,76,0,75,0,98,76,0,75,0,97,76,0,75,0,96,76,0,75,0,95,76,
  //   0,75,0,94,76,0,75,0,93,76,0,75,0,92,76,0,75,0,91,76,0,75,0,90,76,0,75,0,8f,76,0,75,
  //   0,8e,76,0,75,0,8d,76,0,75,0,8c,76,0,75,0,8b,76,0,75,0,8a,76,0,75,0,89,76,0,75,0,88,
  //   76,0,75,0,87,76,0,75,0,86,76,0,75,0,85,76,0,75,0,84,76,0,75,0,83,76,0,75,0,82,76,
  //   0,75,0,81,76,0,75,0,80,76,0,75,0,7f,76,0,75,0,7e,76,0,75,0,7d,76,0,75,0,7c,76,0,75,
  //   0,7b,76,0,75,0,7a,76,0,75,0,79,76,0,75,0,78,76,0,75,0,77,76,0,75,0,76,76,0,75,0,75,
  //   76,0,75,0,74,76,0,75,0,73,76,0,75,0,72,76,0,75,0,71,76,0,75,0,70,76,0,75,0,6f,76,
  //   0,75,0,6e,76,0,75,0,6d,76,0,75,0,6c,76,0,75,0,6b,76,0,75,0,6a,76,0,75,0,69,76,0,75,
  //   0,68,76,0,75,0,67,76,0,75,0,66,76,0,75,0,65,76,0,75,0,64,76,0,75,0,63,76,0,75,0,62,
  //   76,0,75,0,61,76,0,75,0,60,76,0,75,0,5f,76,0,75,0,5e,76,0,75,0,5d,76,0,75,0,5c,76,
  //   0,75,0,5b,76,0,75,0,5a,76,0,75,0,59,76,0,75,0,58,76,0,75,0,57,76,0,75,0,56,76,0,75,
  //   0,55,76,0,75,0,54,76,0,75,0,53,76,0,75,0,52,76,0,75,0,51,76,0,75,0,50,76,0,75,0,4f,
  //   76,0,75,0,4e,76,0,75,0,4d,76,0,75,0,4c,76,0,75,0,4b,76,0,75,0,4a,76,0,75,0,49,76,
  //   0,75,0,48,76,0,75,0,47,76,0,75,0,46,76,0,75,0,45,76,0,75,0,44,76,0,75,0,43,76,0,75,
  //   0,42,76,0,75,0,41,76,0,75,0,40,76,0,75,0,3f,76,0,75,0,3e,76,0,75,0,3d,76,0,75,0,3c,
  //   76,0,75,0,3b,76,0,75,0,3a,76,0,75,0,39,76,0,75,0,38,76,0,75,0,37,76,0,75,0,36,76,
  //   0,75,0,35,76,0,75,0,34,76,0,75,0,33,76,0,75,0,32,76,0,75,0,31,76,0,75,0,30,76,0,75,
  //   0,2f,76,0,75,0,2e,76,0,75,0,2d,76,0,75,0,2c,76,0,75,0,2b,76,0,75,0,2a,76,0,75,0,29,
  //   76,0,75,0,28,76,0,75,0,27,76,0,75,0,26,76,0,75,0,25,76,0,75,0,24,76,0,75,0,23,76,
  //   0,75,0,22,76,0,75,0,21,76,0,75,0,20,76,0,75,0,1f,76,0,75,0,1e,76,0,75,0,1d,76,0,75,
  //   0,1c,76,0,75,0,1b,76,0,75,0,1a,76,0,75,0,19,76,0,75,0,18,76,0,75,0,17,76,0,75,0,16,
  //   76,0,75,0,15,76,0,75,0,14,76,0,75,0,13,76,0,75,0,12,76,0,75,0,11,76,0,75,0,10,76,
  //   0,75,0,f,76,0,75,0,e,76,0,75,0,d,76,0,75,0,c,76,0,75,0,b,76,0,75,0,a,76,0,75,0,9,
  //   76,0,75,0,8,76,0,75,0,7,76,0,75,0,6,76,0,75,0,5,76,0,75,0,4,76,0,75,0,3,76,0,75,0,
  //   2,76,0,75,0,1,76,0,75,0,0,76,0,75,81,0,75,82,0,75,83,0,75,d0,0,75,e0,0,75,f0,0,75,
  //   82,51,75,83,88,75,e0,45,f0,75,82,b8,75,83,92,75,e0,84,f0,75,82,f4,75,83,8b,75,e0,
  //   63,f0,75,82,87,75,83,5d,75,e0,6f,f0,75,82,c,75,83,1a,75,e0,aa,f0,75,82,f1,75,83,eb,
  //   75,e0,3e,f0,75,82,97,75,83,7,75,e0,f4,f0,75,82,9c,75,83,74,75,e0,4d,f0,75,82,b9,75,
  //   83,8f,75,e0,ae,f0,75,82,61,75,83,54,75,e0,7a,f0,75,82,f0,75,83,6d,75,e0,a,f0,75,82,
  //   46,75,83,1e,75,e0,f7,f0,75,82,1e,75,83,cd,75,e0,e1,f0,75,82,cc,75,83,fa,75,e0,e2,
  //   f0,75,82,a9,75,83,39,75,e0,ea,f0,75,82,4,75,83,3c,75,e0,da,f0,75,82,63,75,83,e,75,
  //   e0,59,f0,75,82,e5,75,83,a6,75,e0,c,f0,75,82,42,75,83,76,75,e0,e0,f0,75,82,a6,75,83,
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  //   core is 6116
  //   L74+LS252
endmodule
