// Digital circuit TOP.dig as structural Verilog
module TOP (
  input  clk,
  input  [11:0] MIPCBI,
  input  MIPCBE,
  input  [15:0] PCBIA1,
  input  PCBE1,
  input  [15:0] PCBIA2,
  input  PCBE2
);

  wire and_1_out, and_2_out, and_3_out, AST_FAIL, button_2_out, button_3_out, button_4_out, CLK_t, CLR,
       comparator_1_eq, comparator_2_eq, comparator_3_eq, core_1_p17, core_1_p18, dipswitch_1_out, DUMP_p5,
       EXIT_p5, IRQ_CAI, nIRQ_OE, nXRAM_OE, nXRAM_WE, or_1_out, RI, SFR_OE, SFR_WE, TI;
  wire [7:0] ADDR_SFR, ADDR_XRAM, BUS_D, INT_irq;
  wire [11:0] MIPC;
  wire [15:0] PC;

  // Probe on PC
  // Probe on MIPC
  Button button_1 (.out(CLR));
  RAMSinglePortSel #(.AddrBits(16), .isProgramMemory("true"), .Bits(8)) XRAM (
    .A({ADDR_SFR, ADDR_XRAM}), .CS(~1'b0), .WE(~nXRAM_WE), .OE(~nXRAM_OE), .D(BUS_D));
  Comparator #(.Bits(12)) comparator_1 (.a(MIPCBI), .b(MIPC), .eq(comparator_1_eq));  // open: gt, lt
  Comparator #(.Bits(16)) comparator_2 (.a(PCBIA1), .b(PC), .eq(comparator_2_eq));  // open: gt, lt
  Comparator #(.Bits(16)) comparator_3 (.a(PCBIA2), .b(PC), .eq(comparator_3_eq));  // open: gt, lt
  and and_1 (and_1_out, comparator_1_eq, MIPCBE);
  and and_2 (and_2_out, comparator_2_eq, PCBE1);
  and and_3 (and_3_out, comparator_3_eq, PCBE2);
  SBUF SBUF (.IO(BUS_D), .CLK(CLK_t), .A(ADDR_SFR), .OE(SFR_OE), .WE(SFR_WE), .RI(RI), .TI(TI));
  DipSwitch dipswitch_1 (.out(dipswitch_1_out));
  Button button_2 (.out(button_2_out));
  Button button_3 (.out(button_3_out));
  Button button_4 (.out(button_4_out));
  or or_1 (or_1_out, and_1_out, and_2_out, and_3_out, AST_FAIL);
  // CORE core_1: pin names not known; wires that end beside it: clk, button_2_out, dipswitch_1_out, button_3_out, button_4_out, CLR, or_1_out, PC, MIPC, BUS_D, {ADDR_SFR, ADDR_XRAM}, nXRAM_WE, nXRAM_OE, CLK_t, nIRQ_OE, IRQ_CAI, core_1_p17, core_1_p18
  INT INT (
    .CLK(CLK_t), .CLR(CLR), .A(ADDR_SFR), .D(BUS_D), .WE(SFR_WE), .OE(SFR_OE), .nIRQ_OE(nIRQ_OE),
    .CAI(IRQ_CAI), .RI(RI), .TI(TI), .IRQ(INT_irq));
  // ASSERT ASSERT: pin names not known; wires that end beside it: and_2_out, CLK_t, BUS_D, ADDR_SFR, SFR_WE, AST_FAIL
  not not_1 (SFR_WE, core_1_p17);
  not not_2 (SFR_OE, core_1_p18);
  // Probe on INT_irq
  // EXTCTL EXIT: pin names not known; wires that end beside it: SFR_WE, ADDR_SFR, BUS_D, CLK_t, EXIT_p5
  // Probe on EXIT_p5
  // DUMP DUMP: pin names not known; wires that end beside it: SFR_WE, ADDR_SFR, BUS_D, CLK_t, DUMP_p5
  // Probe on DUMP_p5

  // Other names for the same wires on the sheet: ADDR_XRAM[15:8] = ADDR_SFR

  // Notes on the sheet:
  //   clk: Hz: 2147483647
  //   contents of ROM (hex, n*v repeats v):
  //   2,a,a2,2,3,14,e8,64,80,f8,e9,33,e8,33,60,11,4,60,f0,ed,33,ec,33,70,9,e8,fc,e9,fd, ea,fe,eb,
  //   ff,22,4,60,de,d3,eb,9f,ea,9e,e9,9d,e8,c2,e7,8c,f0,c2,f7,95,f0,40,c,e8,cc, f8,e9,cd,f9,ea,ce,
  //   fa,eb,cf,fb,12,2,df,85,d0,f0,58,4,70,3,20,d5,b3,e8,4,70,7,50,2, b2,d5,2,3,1e,92,d5,ec,4,60,
  //   f7,e4,cc,c0,e0,c3,98,f8,60,3b,94,18,60,8,40,d,d0,e0,fb, 2,2,f6,e4,fb,fa,c9,fc,80,28,e8,30,e4,
  //   6,e4,c9,fb,e4,ca,fc,e8,30,e3,5,e4,c9,ca,cb,fc, e8,54,7,60,10,f8,c3,e9,13,f9,ea,13,fa,eb,13,
  //   fb,ec,13,fc,d8,f1,30,f5,2f,c3,e4,9c,fc, ef,9b,ff,ee,9a,fe,ed,99,fd,d0,e0,fb,ef,4e,4d,4c,70,
  //   12,22,db,3,2,3,1b,ec,2c,fc,ef, 33,ff,ee,33,fe,ed,33,fd,ed,30,e7,eb,2,2,f6,ef,2b,ff,ee,3a,fe,
  //   ed,39,fd,d0,e0,fb,50, 13,b,bb,0,3,2,3,1e,ed,13,fd,ee,13,fe,ef,13,ff,ec,13,fc,2,2,f6,ec,4d,60,
  //   11,e8,49,70, 17,ed,33,ec,33,4,60,d,e4,fc,ff,fe,fd,22,e9,33,e8,33,4,70,f8,2,3,14,12,2,df,58,
  //   4,60, 9,e4,cc,24,81,50,6,28,50,9,2,3,1e,28,40,3,2,3,1b,c0,e0,eb,4a,70,44,b9,80,6,d0,e0, fb,
  //   2,3,a,ef,4e,70,1c,bd,80,8,eb,ff,ea,fe,e9,fd,80,eb,e9,8d,f0,a4,fe,e5,f0,2,1,e4, e9,cd,f9,ea,
  //   fe,eb,ff,ef,89,f0,a4,fc,e5,f0,ce,89,f0,a4,2e,ff,e4,35,f0,cd,89,f0,a4, 2d,fe,e4,35,f0,80,67,
  //   ef,4e,70,5,bd,80,d7,80,c3,ef,8b,f0,a4,ac,f0,ee,8b,f0,a4,2c,fc, e4,35,f0,f8,ef,8a,f0,a4,2c,e5,
  //   f0,38,fc,e4,33,cb,8d,f0,a4,2c,fc,e5,f0,3b,f8,ee,8a, f0,a4,2c,fc,e5,f0,38,f8,e4,33,cf,89,f0,
  //   a4,2c,fc,e5,f0,38,cf,34,0,ce,89,f0,a4,2f,ff, e5,f0,3e,fe,e4,33,c9,8d,f0,a4,2e,fe,e5,f0,39,cd,
  //   8a,f0,a4,2f,ff,e5,f0,3e,fe,e4,3d, fd,33,d0,e0,fb,50,7,b,bb,0,f,2,3,1e,ec,2c,fc,ef,33,ff,ee,
  //   33,fe,ed,33,fd,2,2,f6,2, 3,1e,ec,5d,4,60,5,e8,59,4,70,3,2,3,14,12,2,df,58,4,60,f6,ec,48,60,
  //   f2,ec,70,4,fd,fe, ff,22,c8,60,db,24,81,c8,50,9,c3,98,60,2,50,6,2,3,1b,98,50,ca,f5,82,e9,29,
  //   4b,4a,70, 5,ab,82,2,3,a,75,f0,0,7c,1a,78,80,c3,ef,9b,ee,9a,ed,99,40,d,c3,ef,9b,ff,ee,9a,fe,
  //    ed,99,fd,e8,42,f0,dc,23,ac,f0,d0,e0,ff,d0,e0,fe,d0,e0,fd,ab,82,20,e7,10,1b,eb,60, ba,ec,2c,
  //   fc,ef,33,ff,ee,33,fe,ed,33,fd,2,2,f6,e8,3,f8,30,e7,5,c0,f0,75,f0,0,ef,2f, ff,ee,33,fe,ed,33,
  //   fd,40,b8,30,e7,c2,80,aa,75,f0,20,80,e,75,f0,10,80,5,75,f0,8,7d, 0,7e,0,7f,0,33,92,d5,30,d5,
  //   3,12,5,23,ec,33,40,10,ef,33,ff,ee,33,fe,ed,33,fd,ec,33, fc,d5,f0,ed,22,e5,f0,24,7e,a2,d5,13,
  //   cc,92,e7,cd,ce,ff,22,e9,d2,e7,c9,33,e8,33,f8, 92,d5,ed,d2,e7,cd,33,ec,33,fc,50,2,b2,d5,22,ec,
  //   30,e7,10,f,bf,0,c,e,be,0,8,d,bd,0, 4,b,eb,60,14,a2,d5,eb,13,fc,ed,92,e7,fd,22,74,ff,fc,fd,fe,
  //   ff,22,e4,80,f8,a2,d5,74, ff,13,fc,7d,80,e4,80,ef,f9,20,e7,28,24,f9,50,3,79,7,e4,f4,24,2,fb,
  //   18,db,fd,e6,24, fb,50,14,e9,60,d,e4,f6,18,e6,4,f6,b4,a,8,e4,f6,d9,f5,74,1,f6,a,22,c2,d5,22,
  //   ed,33, ec,33,92,d5,fa,60,2a,b4,ff,33,ed,c2,e7,7b,ff,60,6,7a,3,79,7d,e4,22,7a,3,79,86,20, d5,
  //   4,7a,3,79,81,22,4e,61,4e,0,2b,49,4e,46,0,2d,49,4e,46,0,e4,7a,8,f6,8,da,fc,7b,0, 74,7,22,e8,
  //   c0,e0,ec,c0,e0,ed,c0,e0,ee,c0,e0,ef,c0,e0,ea,75,f0,10,a4,ca,ab,f0,75,f0, 4d,a4,2b,fb,e4,35,
  //   f0,fc,ea,24,10,fa,eb,34,c5,fb,ec,34,d9,fc,ed,c2,e7,ff,75,f0,56, a4,f4,24,11,c5,f0,f4,34,c5,
  //   8f,f0,a4,2a,e5,f0,3b,e4,3c,f6,20,e7,14,12,4,8b,d0,e0,ff, d0,e0,fe,d0,e0,fd,d0,e0,fc,12,2,4,
  //   80,14,f4,4,12,4,8b,d0,e0,ff,d0,e0,fe,d0,e0,fd,d0, e0,fc,12,0,fb,d0,e0,f8,e6,fa,ed,d2,e7,cd,
  //   33,ec,33,24,82,fb,e4,c3,cf,33,cf,ce,33,ce, cd,33,cd,33,db,f3,7b,7,75,f0,a,84,60,4,f6,8,1b,a,
  //   e5,f0,f6,8,8f,f0,74,a,a4,ff,ac,f0, 8e,f0,74,a,a4,2c,fe,ac,f0,50,1,c,8d,f0,74,a,a4,2c,fd,e4,
  //   35,f0,f6,8,db,de,74,7,22, 3f,80,0,0,41,20,0,0,42,c8,0,0,44,7a,0,0,46,1c,40,0,47,c3,50,0,49,
  //   74,24,0,4b,18,96, 80,4c,be,bc,20,5a,e,1b,ca,67,53,c2,1c,74,9d,c5,ae,fb,60,6,54,7,60,1c,23,23,
  //   12,4,b9, eb,54,38,60,9,12,4,a5,12,4,b4,12,0,fb,ec,f8,ed,f9,ee,fa,ef,cb,22,eb,12,4,b4,80,f1,
  //    54,38,3,24,1c,90,4,5b,fe,93,fc,e,ee,93,fd,e,ee,93,e,ce,93,ff,22,bb,1,6,89,82,8a,83, e0,22,
  //   50,2,e7,22,bb,fe,2,e3,22,89,82,8a,83,e4,93,22,bb,1,c,e5,82,29,f5,82,e5,83,3a, f5,83,e0,22,50,
  //   6,e9,25,82,f8,e6,22,bb,fe,6,e9,25,82,f8,e2,22,e5,82,29,f5,82,e5,83, 3a,f5,83,e4,93,22,bb,1,
  //   6,89,82,8a,83,f0,22,50,2,f7,22,bb,fe,1,f3,22,c3,e4,9f,ff,e4, 9e,fe,e4,9d,fd,e4,9c,fc,22,fa,
  //   e6,fb,8,8,e6,f9,25,f0,f6,18,e6,ca,3a,f6,22,d0,83,d0, 82,f8,e4,93,70,12,74,1,93,70,d,a3,a3,93,
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endmodule
